# Fritzing sketch montage_poc (saved by Fritzing 0.9.6b)
breadboards: 1

parts:
  J2 = Piezo Speaker
  R1 = Resistor [tolerance=±5% resistance=10k package="0603 [SMD]"]
  S2 = Pushbutton [package="[THT]"]
  M1 = DOIT Esp32 DevKit v1 (30 pins long, 11 pins width) [part_number=ESP32S-PIN30]
  J3 = Basic Servo
  Matrix_keypad1 = KEYPAD 4x4
  R2 = Resistor [tolerance=±5% resistance=1k package="0603 [SMD]"]
  R3 = Resistor [tolerance=±5% resistance=1k package="0603 [SMD]"]
  LED1 = RGB LED (com. cathode, rgb) [package="5 mm [THT]"]
  R4 = Resistor [tolerance=±5% resistance=1k package="0603 [SMD]"]
  Part2 = LCD1602-I2C

nets:
  GND: J2.pin1, R1.Pin_0, M1.GND, J3.gnd, LED1.red_anode, LED1.common_cathode, LED1.green_anode, LED1.blue_anode, Part2.GND
  N1: J2.pin2, M1.RX2
  N2: R1.Pin_1, S2.Pin_3, S2.Pin_4, M1.D4
  VCC: S2.Pin_1, S2.Pin_2, M1.3V3, J3.vcc, Part2.VCC
  N3: M1.D15, J3.pulse
  N4: M1.D5, Matrix_keypad1.col3
  N5: M1.D18, Matrix_keypad1.col4
  N6: M1.D21, Part2.SDA
  N7: M1.D22, Part2.SCL
  N8: M1.D23, M1.D13, R4.Pin_1
  N9: M1.D32, Matrix_keypad1.col1
  N10: M1.D33, Matrix_keypad1.col2
  N11: M1.D25, Matrix_keypad1.row1
  N12: M1.D26, Matrix_keypad1.row2
  N13: M1.D27, Matrix_keypad1.row3
  N14: M1.D14, Matrix_keypad1.row4
  N15: R2.Pin_0, R3.Pin_0
  N16: R2.Pin_1, R3.Pin_1

custom parts:
  DOIT Esp32 DevKit v1 (30 pins long, 11 pins width): The DOIT Esp32 DevKit v1 is one of the development board created by DOIT to evaluate the ESP-WROOM-32 module. It is based on the ESP32 microcontroller that boasts Wifi, Bluetooth, Ethernet and Low Power support all in a single chip. (vanepp) made breadboard work, adjusted pin numbering and labels and reduced size of schematic and cleaned up pcb. This chip is 30pins long (2 x15) and 11 pins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
  KEYPAD 4x4: Matrix keypad 16 buttons, 4 rows x 4 columns
  LCD1602-I2C: A standard character display, usually with 2x16 characters. Comes in many colors with LCM1602 IIC attached.
